// Logisim project ananthudsd.circ as structural Verilog: 2 circuits, main circuit main
module main (
  input  B3,
  input  A3,
  input  B2,
  input  A2,
  input  B1,
  input  A1,
  input  B0,
  input  A0,
  input  C0,
  output C4,
  output S3,
  output S2,
  output S1,
  output S0
);

  wire and_1_out, and_2_out, and_3_out, and_4_out, carry_1_c1, carry_1_c2, carry_1_c3, xor_1_out, xor_2_out,
       xor_3_out;

  xor xor_1 (xor_1_out, B3, A3);
  and and_1 (and_1_out, B3, A3);
  xor xor_2 (xor_2_out, B2, A2);
  and and_2 (and_2_out, B2, A2);
  xor xor_3 (xor_3_out, B1, A1);
  and and_3 (and_3_out, B1, A1);
  xor xor_4 (S0, B0, A0);
  and and_4 (and_4_out, B0, A0);
  CARRY carry_1 (
    .P3(xor_1_out), .G3(and_1_out), .P2(xor_2_out), .G2(and_2_out), .P1(xor_3_out), .G1(and_3_out), .P0(S0),
    .G0(and_4_out), .C0(C0), .C4(C4), .C3(carry_1_c3), .C2(carry_1_c2), .C1(carry_1_c1));
  xor xor_5 (S3, xor_1_out, carry_1_c3);
  xor xor_6 (S2, xor_2_out, carry_1_c2);
  xor xor_7 (S1, xor_3_out, carry_1_c1);
  Hex_Digit_Display hex_digit_display_1 (.value({{3{C0}}, C4}));  // open: dp
  Hex_Digit_Display hex_digit_display_2 (.value({S3, S2, S1, S0}));  // open: dp
endmodule

module CARRY (
  input  P3,
  input  G3,
  input  P2,
  input  G2,
  input  P1,
  input  G1,
  input  P0,
  input  G0,
  input  C0,
  output C4,
  output C3,
  output C2,
  output C1
);

  wire or_1_out, or_2_out, P0C0_out, P1G0_out, P1P0C0_out, P2G1_out, P2P1G0_out, P2P1P0C0_out, P3G2_out,
       P3P2G1_out, P3P2P1G0_out, P3P2P1P0C0_out;

  and P3G2 (P3G2_out, P3, G2);
  and P3P2G1 (P3P2G1_out, P3, P2);
  and P3P2P1G0 (P3P2P1G0_out, P3, P2, P1, G0);
  and P3P2P1P0C0 (P3P2P1P0C0_out, P3, P2, P1, P0, C0);
  and P2G1 (P2G1_out, P2, G1);
  and P2P1G0 (P2P1G0_out, P2, G0, P1);
  and P2P1P0C0 (P2P1P0C0_out, P2, P1, P0, C0);
  and P1G0 (P1G0_out, P1, G0);
  and P1P0C0 (P1P0C0_out, P1, C0, P0);
  and P0C0 (P0C0_out, P0, C0);
  or or_1 (or_1_out, P3G2_out, P3P2G1_out);
  or or_2 (or_2_out, P3P2P1G0_out, P3P2P1P0C0_out);
  or or_3 (C3, P2G1_out, G2, P2P1P0C0_out, P2P1G0_out);
  or or_4 (C2, P1G0_out, G1, P1P0C0_out);
  or or_5 (C1, P0C0_out, G0);
  or or_6 (C4, or_1_out, or_2_out, G3);
endmodule
